// Logisim project LogisimTPGroupe7.circ as structural Verilog: 3 circuits, main circuit circ2
module circ2 (
  input  A,
  input  B,
  input  C,
  input  D,
  output Q
);

  wire not_1_out;

  not not_1 (not_1_out, B);
  and and_1 (Q, A, not_1_out, C);
endmodule

module circ1 (
  input  A,
  input  B,
  input  C,
  input  D,
  output Q
);

  wire and_1_out, and_2_out, and_3_out, and_4_out, and_5_out, and_6_out, and_7_out, not_1_out, not_2_out,
       not_3_out, not_4_out, not_5_out, or_1_out, or_2_out;

  not not_1 (not_1_out, B);
  not not_2 (not_2_out, D);
  not not_3 (not_3_out, C);
  not not_4 (not_4_out, A);
  not not_5 (not_5_out, B);
  and and_1 (and_1_out, A, not_2_out);
  or or_1 (or_1_out, B, not_3_out);
  or or_2 (or_2_out, not_4_out, D);
  and and_2 (and_2_out, not_5_out, C);
  and and_3 (and_3_out, A, not_1_out);
  and and_4 (and_4_out, and_1_out, or_1_out);
  and and_5 (and_5_out, or_2_out, and_2_out);
  and and_6 (and_6_out, and_3_out, C);
  and and_7 (and_7_out, and_4_out, and_5_out);
  or or_3 (Q, and_6_out, and_7_out);
endmodule

module circ3 (
  input  A,
  input  B,
  input  C,
  input  D,
  output Q
);

  wire circ1_1_q, circ2_1_q, not_1_out;

  circ1 circ1_1 (.A(A), .B(B), .C(C), .D(D), .Q(circ1_1_q));
  circ2 circ2_1 (.A(A), .B(B), .C(C), .D(D), .Q(circ2_1_q));
  not not_1 (not_1_out, circ2_1_q);
  and and_1 (Q, circ1_1_q, not_1_out);
endmodule
